// Logisim project 32bit_pipeline_cpu.circ as structural Verilog: 12 circuits, main circuit main
module main (
);

  wire and_3_out, and_6_out, CLK, data_hazard_1_dhs, dof_ex_1_mwex, dof_ex_1_psex, dof_ex_1_rwex,
       ex_wb_1_rwwb, ex_wb_1_stlwb, function_unit_1_n, function_unit_1_v, function_unit_1_z,
       instruction_decoder_1_cs, instruction_decoder_1_ma, instruction_decoder_1_mb,
       instruction_decoder_1_mw, instruction_decoder_1_ps, instruction_decoder_1_rw, not_1_out, not_2_out,
       not_3_out, or_1_out, or_2_out, xor_1_out, xor_2_out;
  wire [0:0] and_1_out;
  wire [1:0] and_5_out, bit_extender_2_out, bit_extender_4_out, dof_ex_1_bsex, dof_ex_1_mdex, ex_wb_1_mdwb,
       instruction_decoder_1_bs, instruction_decoder_1_md;
  wire [3:0] dof_ex_1_fsex, instruction_decoder_1_fs;
  wire [4:0] and_4_out, bit_extender_3_out, dof_ex_1_daex, dof_ex_1_shex, ex_wb_1_dawb,
       instruction_decoder_1_aa, instruction_decoder_1_ba, instruction_decoder_1_da;
  wire [31:0] adder_1_out, adder_32bit_1_out, and_2_out, bit_extender_1_out, bit_extender_5_out,
       constant_unit_1_im_output, dof_ex_1_busaex, dof_ex_1_busbex, dof_ex_1_pcex, ex_wb_1_fwb,
       ex_wb_1_memreadwb, function_unit_1_f, if_dof_1_instdof, if_dof_1_pcdof, multiplexer_1_out,
       multiplexer_2_out, multiplexer_3_out, multiplexer_4_out, PC_q, ram_1_data, register_file_1_ra,
       register_file_1_rb, rom_1_data;

  or or_1 (or_1_out, dof_ex_1_bsex[1], xor_1_out);
  xor xor_1 (xor_1_out, dof_ex_1_psex, function_unit_1_z);
  Clock clock_1 (.out(CLK));
  and and_1 (and_1_out[0], dof_ex_1_bsex[0], or_1_out);
  or or_2 (or_2_out, dof_ex_1_bsex[1], and_1_out[0]);
  Multiplexer #(.select(2), .width(32), .enable("false")) multiplexer_1 (
    .in0(adder_1_out), .in1(adder_32bit_1_out), .in2(dof_ex_1_busaex), .in3(adder_32bit_1_out),
    .out(multiplexer_1_out), .sel({dof_ex_1_bsex[1], and_1_out[0]}));
  Register #(.width(32)) PC (.D(multiplexer_1_out), .en(not_2_out), .Q(PC_q), .clk(CLK));  // open: clr
  not not_1 (not_1_out, or_2_out);
  assign bit_extender_1_out = {{31{not_1_out}}, not_1_out};  // Bit_Extender bit_extender_1
  Adder #(.width(32)) adder_1 (.a(PC_q), .b(32'h1), .out(adder_1_out));  // open: cin, cout
  ROM #(.addrWidth(24), .dataWidth(32)) rom_1 (.addr(PC_q[23:0]), .data(rom_1_data));  // open: sel
  assign and_2_out = bit_extender_1_out & rom_1_data;  // AND_Gate and_2, 32 bits wide
  IF_DOF if_dof_1 (
    .INSTIF(and_2_out), .PCIF(adder_1_out), .INSTDOF(if_dof_1_instdof), .PCDOF(if_dof_1_pcdof), .CLK(CLK),
    .CLR(1'b0), .EN(not_2_out));
  Instruction_decoder instruction_decoder_1 (
    .Inst(if_dof_1_instdof), .BA(instruction_decoder_1_ba), .AA(instruction_decoder_1_aa),
    .DA(instruction_decoder_1_da), .MD(instruction_decoder_1_md), .BS(instruction_decoder_1_bs),
    .MW(instruction_decoder_1_mw), .FS(instruction_decoder_1_fs), .MA(instruction_decoder_1_ma),
    .RW(instruction_decoder_1_rw), .PS(instruction_decoder_1_ps), .MB(instruction_decoder_1_mb),
    .CS(instruction_decoder_1_cs));
  Constant_unit constant_unit_1 (
    .Im_input(if_dof_1_instdof[14:0]), .Im_output(constant_unit_1_im_output), .CS(instruction_decoder_1_cs));
  Register_file register_file_1 (
    .AA(instruction_decoder_1_aa), .RA(register_file_1_ra), .BA(instruction_decoder_1_ba), .DA(ex_wb_1_dawb),
    .RW(ex_wb_1_rwwb), .CLK(CLK), .RB(register_file_1_rb), .CLR(1'b0), .DIN(multiplexer_4_out));
  Multiplexer #(.width(32), .enable("false")) multiplexer_2 (
    .in0(register_file_1_ra), .in1(if_dof_1_pcdof), .out(multiplexer_2_out), .sel(instruction_decoder_1_ma));
  Multiplexer #(.width(32), .enable("false")) multiplexer_3 (
    .in0(register_file_1_rb), .in1(constant_unit_1_im_output), .out(multiplexer_3_out),
    .sel(instruction_decoder_1_mb));
  and and_3 (and_3_out, not_2_out, not_1_out, instruction_decoder_1_rw);
  assign and_4_out = instruction_decoder_1_da & bit_extender_3_out;  // AND_Gate and_4, 5 bits wide
  assign and_5_out = instruction_decoder_1_bs & bit_extender_4_out & bit_extender_2_out;  // AND_Gate and_5, 2 bits wide
  assign bit_extender_2_out = {{1{not_1_out}}, not_1_out};  // Bit_Extender bit_extender_2
  and and_6 (and_6_out, instruction_decoder_1_mw, not_1_out, not_2_out);
  assign bit_extender_3_out = {{4{not_2_out}}, not_2_out};  // Bit_Extender bit_extender_3
  assign bit_extender_4_out = {{1{not_2_out}}, not_2_out};  // Bit_Extender bit_extender_4
  DOF_EX dof_ex_1 (
    .PCDOF(if_dof_1_pcdof), .SHDOF(if_dof_1_instdof[4:0]), .FSDOF(instruction_decoder_1_fs),
    .BUSADOF(multiplexer_2_out), .MWDOF(and_6_out), .PSDOF(instruction_decoder_1_ps),
    .BUSBDOF(multiplexer_3_out), .BSDOF(and_5_out), .MDDOF(instruction_decoder_1_md), .DADOF(and_4_out),
    .RWDOF(and_3_out), .PCEX(dof_ex_1_pcex), .SHEX(dof_ex_1_shex), .FSEX(dof_ex_1_fsex),
    .BUSAEX(dof_ex_1_busaex), .MWEX(dof_ex_1_mwex), .PSEX(dof_ex_1_psex), .BUSBEX(dof_ex_1_busbex),
    .BSEX(dof_ex_1_bsex), .MDEX(dof_ex_1_mdex), .DAEX(dof_ex_1_daex), .RWEX(dof_ex_1_rwex), .CLK(CLK),
    .CLR(1'b0), .EN(not_2_out));
  Adder_32bit adder_32bit_1 (.RA(dof_ex_1_busbex), .RB(dof_ex_1_pcex), .OUT(adder_32bit_1_out));  // open: V, in_3
  Function_unit function_unit_1 (
    .RA(dof_ex_1_busaex), .RB(dof_ex_1_busbex), .FS(dof_ex_1_fsex), .Shift(dof_ex_1_shex),
    .N(function_unit_1_n), .V(function_unit_1_v), .Z(function_unit_1_z), .F(function_unit_1_f));
  xor xor_2 (xor_2_out, function_unit_1_v, function_unit_1_n);
  not not_2 (not_2_out, data_hazard_1_dhs);
  Data_hazard data_hazard_1 (
    .MBDOF(instruction_decoder_1_mb), .MADOF(instruction_decoder_1_ma), .RWEX(dof_ex_1_rwex),
    .DHS(data_hazard_1_dhs), .BADOF(instruction_decoder_1_ba), .AADOF(instruction_decoder_1_aa),
    .DAEX(dof_ex_1_daex), .DAWB(ex_wb_1_dawb), .RWWB(ex_wb_1_rwwb));
  not not_3 (not_3_out, dof_ex_1_mwex);
  RAM #(.addrWidth(24), .dataWidth(32), .bus("separate")) ram_1 (
    .addr(dof_ex_1_busaex[23:0]), .din(dof_ex_1_busbex), .data(ram_1_data), .str(dof_ex_1_mwex), .clk(CLK),
    .ld(not_3_out));  // open: sel, clr
  EX_WB ex_wb_1 (
    .SLTEX(xor_2_out), .MDEX(dof_ex_1_mdex), .DAEX(dof_ex_1_daex), .FEX(function_unit_1_f),
    .RWEX(dof_ex_1_rwex), .MEMREADEX(ram_1_data), .STLWB(ex_wb_1_stlwb), .MDWB(ex_wb_1_mdwb),
    .DAWB(ex_wb_1_dawb), .FWB(ex_wb_1_fwb), .RWWB(ex_wb_1_rwwb), .MEMREADWB(ex_wb_1_memreadwb), .CLK(CLK),
    .CLR(1'b0), .EN(1'b1));
  assign bit_extender_5_out = {{31{1'b0}}, ex_wb_1_stlwb};  // Bit_Extender bit_extender_5
  Multiplexer #(.select(2), .width(32)) multiplexer_4 (
    .in0(ex_wb_1_fwb), .in1(ex_wb_1_memreadwb), .in2(bit_extender_5_out), .out(multiplexer_4_out),
    .sel(ex_wb_1_mdwb), .en(ex_wb_1_rwwb));  // open: in3

  // Notes on the sheet:
  //   contents of rom_1 (hex, n*v repeats v):
  //   442014a6 80810000 4f12000
endmodule

// Adder
module Adder_32bit (
  input  [31:0] RA,
  input  [31:0] RB,
  input  in_3,
  output [31:0] OUT,
  output V
);

  wire adder_1_cout, adder_2_cout;

  Adder #(.width(31)) adder_1 (.a(RA[30:0]), .b(RB[30:0]), .out(OUT[30:0]), .cin(in_3), .cout(adder_1_cout));
  Adder #(.width(1)) adder_2 (.a(RA[31]), .b(RB[31]), .out(OUT[31]), .cin(adder_1_cout), .cout(adder_2_cout));
  xor xor_1 (V, adder_1_cout, adder_2_cout);

  // Other names for the same wires on the sheet: A[31:0] = RA; B[31:0] = RB; CIN = in_3; Overflow = V
endmodule

// Sub
module Subtractor_32bit (
  input  [31:0] RA,
  input  [31:0] RB,
  input  in_3,
  output [31:0] OUT,
  output V
);

  wire subtractor_1_bout, subtractor_2_bout;

  Subtractor #(.width(31)) subtractor_1 (
    .a(RA[30:0]), .b(RB[30:0]), .out(OUT[30:0]), .bin(in_3), .bout(subtractor_1_bout));
  Subtractor #(.width(1)) subtractor_2 (
    .a(RA[31]), .b(RB[31]), .out(OUT[31]), .bin(subtractor_1_bout), .bout(subtractor_2_bout));
  xor xor_1 (V, subtractor_1_bout, subtractor_2_bout);

  // Other names for the same wires on the sheet: A[31:0] = RA; B[31:0] = RB; BIN = in_3; Overflow = V
endmodule

// Opcode Decoder
module Opcode_decoder (
  input  [6:0] OP,
  output [1:0] MD,
  output [1:0] BS,
  output MW,
  output [3:0] FS,
  output MA,
  output RW,
  output PS,
  output MB,
  output CS
);

  wire and_3_out, and_4_out, and_5_out, and_6_out, and_7_out, and_8_out, and_9_out, and_11_out, and_13_out,
       and_14_out, and_15_out, and_16_out, and_17_out, and_18_out, and_19_out, and_20_out, and_21_out,
       and_22_out, and_23_out, and_24_out, and_25_out, and_26_out, and_27_out, and_28_out, and_29_out,
       and_30_out, and_31_out, and_32_out, and_34_out, and_35_out, and_36_out, and_37_out, and_38_out,
       and_39_out, and_40_out, and_41_out, and_42_out, and_43_out, and_44_out, and_45_out, and_46_out,
       and_47_out, and_48_out, and_49_out, and_50_out, and_51_out, and_52_out, not_1_out, not_2_out,
       not_3_out, not_4_out, not_5_out, not_6_out, not_7_out, not_8_out, not_9_out, not_10_out, not_11_out,
       not_12_out, not_13_out, not_14_out, not_15_out, not_16_out, not_17_out, not_18_out, not_19_out,
       not_20_out, not_21_out, not_22_out, not_23_out, not_24_out, not_25_out, not_26_out, not_27_out,
       not_28_out, not_29_out, not_30_out, not_31_out, not_32_out, not_33_out, not_34_out, not_35_out,
       not_36_out, not_37_out, not_38_out, not_39_out, not_40_out, not_41_out, not_42_out, not_43_out,
       not_44_out, not_45_out, not_46_out, not_47_out, not_48_out, not_49_out, not_50_out, not_51_out,
       not_52_out, not_53_out, not_54_out, not_55_out, not_56_out, not_57_out, not_58_out, not_59_out,
       not_60_out, not_61_out, not_62_out, not_63_out, not_64_out, not_65_out, not_66_out, not_67_out,
       not_68_out, not_69_out, not_70_out, not_71_out, not_72_out, not_73_out, not_74_out, not_75_out,
       not_76_out, not_77_out, not_78_out, not_79_out, not_80_out, not_81_out, not_82_out, not_83_out,
       not_84_out, not_85_out, not_86_out, not_87_out, not_88_out, not_89_out, not_90_out, not_91_out,
       not_92_out, not_93_out, not_94_out, not_95_out, not_96_out, not_97_out, not_98_out, not_99_out,
       not_100_out, not_101_out, not_102_out, not_103_out, not_104_out, not_105_out, not_106_out,
       not_107_out, not_108_out, not_109_out, not_110_out, not_111_out, not_112_out, not_113_out,
       not_114_out, not_115_out, not_116_out, not_117_out, not_118_out, not_119_out, not_120_out,
       not_121_out, not_122_out, not_123_out, not_124_out, not_125_out, not_126_out, not_127_out,
       not_128_out, not_129_out, not_130_out, not_131_out, not_132_out, not_133_out, not_134_out,
       not_135_out, not_136_out, not_137_out, not_138_out, not_139_out, not_140_out, not_141_out,
       not_142_out, not_143_out, not_144_out, not_145_out, not_146_out, not_147_out, not_148_out,
       not_149_out, not_150_out, not_151_out, not_152_out, not_153_out, not_154_out, not_155_out,
       not_156_out, not_157_out, not_158_out, not_159_out, not_160_out, not_161_out, not_162_out,
       not_163_out, not_164_out, not_165_out, not_166_out, not_167_out, not_168_out, not_169_out,
       not_170_out, not_171_out, not_172_out, not_173_out, not_174_out, not_175_out, not_176_out,
       not_177_out, not_178_out, not_179_out, not_180_out, not_181_out, not_182_out, not_183_out,
       not_184_out, not_185_out, not_186_out, not_187_out, not_188_out, not_189_out, not_190_out,
       not_191_out, not_192_out, not_193_out, not_194_out, not_195_out, not_196_out, not_197_out,
       not_198_out, not_199_out, not_200_out, not_201_out, not_202_out, not_203_out, not_204_out,
       not_205_out, not_206_out, not_207_out, not_208_out, not_209_out, not_210_out, not_211_out,
       not_212_out, not_213_out, not_214_out, not_215_out, not_216_out, not_217_out, not_218_out,
       not_219_out, not_220_out, not_221_out, not_222_out, not_223_out, not_224_out, not_225_out,
       not_226_out, not_227_out, not_228_out, not_229_out, not_230_out, not_231_out, not_232_out,
       not_233_out, not_234_out, not_235_out, not_236_out;

  not not_1 (not_1_out, OP[0]);
  not not_2 (not_2_out, OP[1]);
  not not_3 (not_3_out, OP[2]);
  not not_4 (not_4_out, OP[3]);
  not not_5 (not_5_out, OP[5]);
  not not_6 (not_6_out, OP[6]);
  not not_7 (not_7_out, OP[1]);
  not not_8 (not_8_out, OP[3]);
  not not_9 (not_9_out, OP[4]);
  not not_10 (not_10_out, OP[0]);
  not not_11 (not_11_out, OP[1]);
  not not_12 (not_12_out, OP[2]);
  not not_13 (not_13_out, OP[3]);
  not not_14 (not_14_out, OP[4]);
  not not_15 (not_15_out, OP[0]);
  not not_16 (not_16_out, OP[1]);
  not not_17 (not_17_out, OP[2]);
  not not_18 (not_18_out, OP[4]);
  not not_19 (not_19_out, OP[5]);
  not not_20 (not_20_out, OP[0]);
  not not_21 (not_21_out, OP[1]);
  not not_22 (not_22_out, OP[2]);
  not not_23 (not_23_out, OP[4]);
  not not_24 (not_24_out, OP[0]);
  not not_25 (not_25_out, OP[1]);
  not not_26 (not_26_out, OP[2]);
  not not_27 (not_27_out, OP[3]);
  not not_28 (not_28_out, OP[6]);
  not not_29 (not_29_out, OP[0]);
  not not_30 (not_30_out, OP[1]);
  not not_31 (not_31_out, OP[2]);
  not not_32 (not_32_out, OP[3]);
  not not_33 (not_33_out, OP[0]);
  not not_34 (not_34_out, OP[1]);
  not not_35 (not_35_out, OP[2]);
  not not_36 (not_36_out, OP[4]);
  not not_37 (not_37_out, OP[0]);
  not not_38 (not_38_out, OP[1]);
  not not_39 (not_39_out, OP[2]);
  not not_40 (not_40_out, OP[3]);
  not not_41 (not_41_out, OP[6]);
  not not_42 (not_42_out, OP[0]);
  not not_43 (not_43_out, OP[1]);
  not not_44 (not_44_out, OP[2]);
  not not_45 (not_45_out, OP[3]);
  not not_46 (not_46_out, OP[4]);
  not not_47 (not_47_out, OP[6]);
  not not_48 (not_48_out, OP[0]);
  not not_49 (not_49_out, OP[1]);
  not not_50 (not_50_out, OP[2]);
  not not_51 (not_51_out, OP[4]);
  not not_52 (not_52_out, OP[5]);
  not not_53 (not_53_out, OP[0]);
  not not_54 (not_54_out, OP[1]);
  not not_55 (not_55_out, OP[2]);
  not not_56 (not_56_out, OP[3]);
  not not_57 (not_57_out, OP[6]);
  not not_58 (not_58_out, OP[0]);
  not not_59 (not_59_out, OP[1]);
  not not_60 (not_60_out, OP[2]);
  not not_61 (not_61_out, OP[3]);
  not not_62 (not_62_out, OP[4]);
  not not_63 (not_63_out, OP[5]);
  not not_64 (not_64_out, OP[0]);
  not not_65 (not_65_out, OP[2]);
  not not_66 (not_66_out, OP[3]);
  not not_67 (not_67_out, OP[4]);
  not not_68 (not_68_out, OP[5]);
  not not_69 (not_69_out, OP[6]);
  not not_70 (not_70_out, OP[1]);
  not not_71 (not_71_out, OP[3]);
  not not_72 (not_72_out, OP[4]);
  not not_73 (not_73_out, OP[5]);
  not not_74 (not_74_out, OP[6]);
  not not_75 (not_75_out, OP[0]);
  not not_76 (not_76_out, OP[1]);
  not not_77 (not_77_out, OP[2]);
  not not_78 (not_78_out, OP[4]);
  not not_79 (not_79_out, OP[5]);
  not not_80 (not_80_out, OP[6]);
  not not_81 (not_81_out, OP[1]);
  not not_82 (not_82_out, OP[2]);
  not not_83 (not_83_out, OP[4]);
  not not_84 (not_84_out, OP[5]);
  not not_85 (not_85_out, OP[6]);
  not not_86 (not_86_out, OP[0]);
  not not_87 (not_87_out, OP[2]);
  not not_88 (not_88_out, OP[4]);
  not not_89 (not_89_out, OP[5]);
  not not_90 (not_90_out, OP[6]);
  not not_91 (not_91_out, OP[2]);
  not not_92 (not_92_out, OP[4]);
  not not_93 (not_93_out, OP[5]);
  not not_94 (not_94_out, OP[6]);
  not not_95 (not_95_out, OP[0]);
  not not_96 (not_96_out, OP[2]);
  not not_97 (not_97_out, OP[3]);
  not not_98 (not_98_out, OP[4]);
  not not_99 (not_99_out, OP[6]);
  not not_100 (not_100_out, OP[1]);
  not not_101 (not_101_out, OP[3]);
  not not_102 (not_102_out, OP[4]);
  not not_103 (not_103_out, OP[6]);
  not not_104 (not_104_out, OP[0]);
  not not_105 (not_105_out, OP[1]);
  not not_106 (not_106_out, OP[2]);
  not not_107 (not_107_out, OP[4]);
  not not_108 (not_108_out, OP[6]);
  not not_109 (not_109_out, OP[1]);
  not not_110 (not_110_out, OP[2]);
  not not_111 (not_111_out, OP[4]);
  not not_112 (not_112_out, OP[6]);
  not not_113 (not_113_out, OP[0]);
  not not_114 (not_114_out, OP[2]);
  not not_115 (not_115_out, OP[4]);
  not not_116 (not_116_out, OP[6]);
  not not_117 (not_117_out, OP[0]);
  not not_118 (not_118_out, OP[2]);
  not not_119 (not_119_out, OP[3]);
  not not_120 (not_120_out, OP[4]);
  not not_121 (not_121_out, OP[5]);
  not not_122 (not_122_out, OP[1]);
  not not_123 (not_123_out, OP[3]);
  not not_124 (not_124_out, OP[4]);
  not not_125 (not_125_out, OP[5]);
  not not_126 (not_126_out, OP[0]);
  not not_127 (not_127_out, OP[1]);
  not not_128 (not_128_out, OP[4]);
  not not_129 (not_129_out, OP[5]);
  not not_130 (not_130_out, OP[6]);
  not not_131 (not_131_out, OP[1]);
  not not_132 (not_132_out, OP[4]);
  not not_133 (not_133_out, OP[5]);
  not not_134 (not_134_out, OP[6]);
  not not_135 (not_135_out, OP[0]);
  not not_136 (not_136_out, OP[4]);
  not not_137 (not_137_out, OP[5]);
  not not_138 (not_138_out, OP[6]);
  not not_139 (not_139_out, OP[0]);
  not not_140 (not_140_out, OP[1]);
  not not_141 (not_141_out, OP[2]);
  not not_142 (not_142_out, OP[3]);
  not not_143 (not_143_out, OP[5]);
  not not_144 (not_144_out, OP[6]);
  not not_145 (not_145_out, OP[1]);
  not not_146 (not_146_out, OP[3]);
  not not_147 (not_147_out, OP[4]);
  not not_148 (not_148_out, OP[0]);
  not not_149 (not_149_out, OP[1]);
  not not_150 (not_150_out, OP[2]);
  not not_151 (not_151_out, OP[3]);
  not not_152 (not_152_out, OP[6]);
  not not_153 (not_153_out, OP[0]);
  not not_154 (not_154_out, OP[1]);
  not not_155 (not_155_out, OP[2]);
  not not_156 (not_156_out, OP[4]);
  not not_157 (not_157_out, OP[5]);
  not not_158 (not_158_out, OP[0]);
  not not_159 (not_159_out, OP[2]);
  not not_160 (not_160_out, OP[3]);
  not not_161 (not_161_out, OP[4]);
  not not_162 (not_162_out, OP[6]);
  not not_163 (not_163_out, OP[1]);
  not not_164 (not_164_out, OP[3]);
  not not_165 (not_165_out, OP[4]);
  not not_166 (not_166_out, OP[6]);
  not not_167 (not_167_out, OP[0]);
  not not_168 (not_168_out, OP[1]);
  not not_169 (not_169_out, OP[2]);
  not not_170 (not_170_out, OP[4]);
  not not_171 (not_171_out, OP[6]);
  not not_172 (not_172_out, OP[1]);
  not not_173 (not_173_out, OP[2]);
  not not_174 (not_174_out, OP[4]);
  not not_175 (not_175_out, OP[6]);
  not not_176 (not_176_out, OP[0]);
  not not_177 (not_177_out, OP[2]);
  not not_178 (not_178_out, OP[4]);
  not not_179 (not_179_out, OP[6]);
  not not_180 (not_180_out, OP[0]);
  not not_181 (not_181_out, OP[2]);
  not not_182 (not_182_out, OP[3]);
  not not_183 (not_183_out, OP[4]);
  not not_184 (not_184_out, OP[5]);
  not not_185 (not_185_out, OP[1]);
  not not_186 (not_186_out, OP[3]);
  not not_187 (not_187_out, OP[4]);
  not not_188 (not_188_out, OP[5]);
  not not_189 (not_189_out, OP[0]);
  not not_190 (not_190_out, OP[1]);
  not not_191 (not_191_out, OP[2]);
  not not_192 (not_192_out, OP[3]);
  not not_193 (not_193_out, OP[4]);
  not not_194 (not_194_out, OP[0]);
  not not_195 (not_195_out, OP[1]);
  not not_196 (not_196_out, OP[2]);
  not not_197 (not_197_out, OP[4]);
  not not_198 (not_198_out, OP[5]);
  not not_199 (not_199_out, OP[0]);
  not not_200 (not_200_out, OP[1]);
  not not_201 (not_201_out, OP[2]);
  not not_202 (not_202_out, OP[4]);
  not not_203 (not_203_out, OP[0]);
  not not_204 (not_204_out, OP[1]);
  not not_205 (not_205_out, OP[2]);
  not not_206 (not_206_out, OP[3]);
  not not_207 (not_207_out, OP[6]);
  not not_208 (not_208_out, OP[0]);
  not not_209 (not_209_out, OP[2]);
  not not_210 (not_210_out, OP[3]);
  not not_211 (not_211_out, OP[4]);
  not not_212 (not_212_out, OP[6]);
  not not_213 (not_213_out, OP[1]);
  not not_214 (not_214_out, OP[3]);
  not not_215 (not_215_out, OP[4]);
  not not_216 (not_216_out, OP[6]);
  not not_217 (not_217_out, OP[0]);
  not not_218 (not_218_out, OP[1]);
  not not_219 (not_219_out, OP[2]);
  not not_220 (not_220_out, OP[3]);
  not not_221 (not_221_out, OP[4]);
  not not_222 (not_222_out, OP[0]);
  not not_223 (not_223_out, OP[1]);
  not not_224 (not_224_out, OP[2]);
  not not_225 (not_225_out, OP[4]);
  not not_226 (not_226_out, OP[5]);
  not not_227 (not_227_out, OP[0]);
  not not_228 (not_228_out, OP[1]);
  not not_229 (not_229_out, OP[2]);
  not not_230 (not_230_out, OP[4]);
  not not_231 (not_231_out, OP[0]);
  not not_232 (not_232_out, OP[1]);
  not not_233 (not_233_out, OP[2]);
  not not_234 (not_234_out, OP[3]);
  not not_235 (not_235_out, OP[6]);
  and and_1 (MD[0], not_1_out, not_2_out, not_3_out, not_4_out, OP[4], not_5_out, not_6_out);
  and and_2 (MD[1], OP[0], not_7_out, OP[2], not_8_out, not_9_out, OP[5], OP[6]);
  and and_3 (and_3_out, not_10_out, not_11_out, not_12_out, not_13_out, not_14_out, OP[5], OP[6]);
  and and_4 (and_4_out, not_15_out, not_16_out, not_17_out, OP[3], not_18_out, not_19_out, OP[6]);
  and and_5 (and_5_out, not_20_out, not_21_out, not_22_out, OP[3], not_23_out, OP[5], OP[6]);
  and and_6 (and_6_out, not_24_out, not_25_out, not_26_out, not_27_out, OP[4], OP[5], not_28_out);
  and and_7 (and_7_out, not_29_out, not_30_out, not_31_out, not_32_out, OP[4], OP[5], OP[6]);
  and and_8 (and_8_out, not_33_out, not_34_out, not_35_out, OP[3], not_36_out, OP[5], OP[6]);
  and and_9 (and_9_out, not_37_out, not_38_out, not_39_out, not_40_out, OP[4], OP[5], not_41_out);
  and and_10 (MW, not_42_out, not_43_out, not_44_out, not_45_out, not_46_out, OP[5], not_47_out);
  and and_11 (and_11_out, not_48_out, not_49_out, not_50_out, OP[3], not_51_out, not_52_out, OP[6]);
  and and_12 (MA, not_53_out, not_54_out, not_55_out, not_56_out, OP[4], OP[5], not_57_out);
  and and_13 (and_13_out, not_58_out, not_59_out, not_60_out, not_61_out, not_62_out, not_63_out, OP[6]);
  and and_14 (and_14_out, not_64_out, OP[1], not_65_out, not_66_out, not_67_out, not_68_out, not_69_out);
  and and_15 (and_15_out, OP[0], not_70_out, OP[2], not_71_out, not_72_out, not_73_out, not_74_out);
  and and_16 (and_16_out, not_75_out, not_76_out, not_77_out, OP[3], not_78_out, not_79_out, not_80_out);
  and and_17 (and_17_out, OP[0], not_81_out, not_82_out, OP[3], not_83_out, not_84_out, not_85_out);
  and and_18 (and_18_out, not_86_out, OP[1], not_87_out, OP[3], not_88_out, not_89_out, not_90_out);
  and and_19 (and_19_out, OP[0], OP[1], not_91_out, OP[3], not_92_out, not_93_out, not_94_out);
  and and_20 (and_20_out, not_95_out, OP[1], not_96_out, not_97_out, not_98_out, OP[5], not_99_out);
  and and_21 (and_21_out, OP[0], not_100_out, OP[2], not_101_out, not_102_out, OP[5], not_103_out);
  and and_22 (and_22_out, not_104_out, not_105_out, not_106_out, OP[3], not_107_out, OP[5], not_108_out);
  and and_23 (and_23_out, OP[0], not_109_out, not_110_out, OP[3], not_111_out, OP[5], not_112_out);
  and and_24 (and_24_out, not_113_out, OP[1], not_114_out, OP[3], not_115_out, OP[5], not_116_out);
  and and_25 (and_25_out, not_117_out, OP[1], not_118_out, not_119_out, not_120_out, not_121_out, OP[6]);
  and and_26 (and_26_out, OP[0], not_122_out, OP[2], not_123_out, not_124_out, not_125_out, OP[6]);
  and and_27 (and_27_out, not_126_out, not_127_out, OP[2], OP[3], not_128_out, not_129_out, not_130_out);
  and and_28 (and_28_out, OP[0], not_131_out, OP[2], OP[3], not_132_out, not_133_out, not_134_out);
  and and_29 (and_29_out, not_135_out, OP[1], OP[2], OP[3], not_136_out, not_137_out, not_138_out);
  and and_30 (and_30_out, not_139_out, not_140_out, not_141_out, not_142_out, OP[4], not_143_out, not_144_out);
  and and_31 (and_31_out, OP[0], not_145_out, OP[2], not_146_out, not_147_out, OP[5], OP[6]);
  and and_32 (and_32_out, not_148_out, not_149_out, not_150_out, not_151_out, OP[4], OP[5], not_152_out);
  and and_33 (PS, not_153_out, not_154_out, not_155_out, OP[3], not_156_out, not_157_out, OP[6]);
  and and_34 (and_34_out, not_158_out, OP[1], not_159_out, not_160_out, not_161_out, OP[5], not_162_out);
  and and_35 (and_35_out, OP[0], not_163_out, OP[2], not_164_out, not_165_out, OP[5], not_166_out);
  and and_36 (and_36_out, not_167_out, not_168_out, not_169_out, OP[3], not_170_out, OP[5], not_171_out);
  and and_37 (and_37_out, OP[0], not_172_out, not_173_out, OP[3], not_174_out, OP[5], not_175_out);
  and and_38 (and_38_out, not_176_out, OP[1], not_177_out, OP[3], not_178_out, OP[5], not_179_out);
  and and_39 (and_39_out, not_180_out, OP[1], not_181_out, not_182_out, not_183_out, not_184_out, OP[6]);
  and and_40 (and_40_out, OP[0], not_185_out, OP[2], not_186_out, not_187_out, not_188_out, OP[6]);
  and and_41 (and_41_out, not_189_out, not_190_out, not_191_out, not_192_out, not_193_out, OP[5], OP[6]);
  and and_42 (and_42_out, not_194_out, not_195_out, not_196_out, OP[3], not_197_out, not_198_out, OP[6]);
  and and_43 (and_43_out, not_199_out, not_200_out, not_201_out, OP[3], not_202_out, OP[5], OP[6]);
  and and_44 (and_44_out, not_203_out, not_204_out, not_205_out, not_206_out, OP[4], OP[5], not_207_out);
  and and_45 (and_45_out, not_208_out, OP[1], not_209_out, not_210_out, not_211_out, OP[5], not_212_out);
  and and_46 (and_46_out, OP[0], not_213_out, OP[2], not_214_out, not_215_out, OP[5], not_216_out);
  and and_47 (and_47_out, not_217_out, not_218_out, not_219_out, not_220_out, not_221_out, OP[5], OP[6]);
  and and_48 (and_48_out, not_222_out, not_223_out, not_224_out, OP[3], not_225_out, not_226_out, OP[6]);
  and and_49 (and_49_out, not_227_out, not_228_out, not_229_out, OP[3], not_230_out, OP[5], OP[6]);
  and and_50 (and_50_out, not_231_out, not_232_out, not_233_out, not_234_out, OP[4], OP[5], not_235_out);
  or or_1 (BS[0], and_3_out, and_4_out, and_5_out, and_6_out);
  not not_236 (not_236_out, and_11_out);
  or or_2 (BS[1], and_7_out, and_8_out, and_9_out);
  and and_51 (and_51_out, OP[3], not_236_out);
  or or_3 (FS[3], and_51_out, and_52_out);
  and and_52 (and_52_out, not_236_out, and_11_out);
  or or_4 (RW, and_13_out, and_14_out, and_15_out, and_16_out, and_17_out, and_18_out, and_19_out, and_20_out, and_21_out, and_22_out, and_23_out, and_24_out, and_25_out, and_26_out, and_27_out, and_28_out, and_29_out, and_30_out, and_31_out, and_32_out);
  or or_5 (MB, and_34_out, and_35_out, and_36_out, and_37_out, and_38_out, and_39_out, and_40_out, and_41_out, and_42_out, and_43_out, and_44_out);
  or or_6 (CS, and_45_out, and_46_out, and_47_out, and_48_out, and_49_out, and_50_out);

  assign FS[2:0] = OP[2:0];
endmodule

module IF_DOF (
  input  CLK,
  input  CLR,
  input  [31:0] INSTIF,
  input  [31:0] PCIF,
  input  EN,
  output [31:0] INSTDOF,
  output [31:0] PCDOF
);

  Register #(.width(32)) register_1 (.D(INSTIF), .en(EN), .Q(INSTDOF), .clk(CLK), .clr(CLR));
  Register #(.width(32)) register_2 (.D(PCIF), .en(EN), .Q(PCDOF), .clk(CLK), .clr(CLR));
endmodule

module DOF_EX (
  input  EN,
  input  CLK,
  input  CLR,
  input  [31:0] PCDOF,
  input  [4:0] SHDOF,
  input  [3:0] FSDOF,
  input  [31:0] BUSADOF,
  input  MWDOF,
  input  PSDOF,
  input  [31:0] BUSBDOF,
  input  [1:0] BSDOF,
  input  [1:0] MDDOF,
  input  [4:0] DADOF,
  input  RWDOF,
  output [31:0] PCEX,
  output [4:0] SHEX,
  output [3:0] FSEX,
  output [31:0] BUSAEX,
  output MWEX,
  output PSEX,
  output [31:0] BUSBEX,
  output [1:0] BSEX,
  output [1:0] MDEX,
  output [4:0] DAEX,
  output RWEX
);

  Register #(.width(32)) register_1 (.D(PCDOF), .en(EN), .Q(PCEX), .clk(CLK), .clr(CLR));
  Register #(.width(32)) register_2 (.D(BUSADOF), .en(1'b1), .Q(BUSAEX), .clk(CLK), .clr(CLR));
  Register #(.width(32)) register_3 (.D(BUSBDOF), .en(1'b1), .Q(BUSBEX), .clk(CLK), .clr(CLR));
  Register #(.width(5)) register_4 (.D(SHDOF), .en(1'b1), .Q(SHEX), .clk(CLK), .clr(CLR));
  Register #(.width(4)) register_5 (.D(FSDOF), .en(1'b1), .Q(FSEX), .clk(CLK), .clr(CLR));
  Register #(.width(1)) register_6 (.D(MWDOF), .en(1'b1), .Q(MWEX), .clk(CLK), .clr(CLR));
  Register #(.width(1)) register_7 (.D(PSDOF), .en(1'b1), .Q(PSEX), .clk(CLK), .clr(CLR));
  Register #(.width(2)) register_8 (.D(BSDOF), .en(1'b1), .Q(BSEX), .clk(CLK), .clr(CLR));
  Register #(.width(2)) register_9 (.D(MDDOF), .en(1'b1), .Q(MDEX), .clk(CLK), .clr(CLR));
  Register #(.width(5)) register_10 (.D(DADOF), .en(1'b1), .Q(DAEX), .clk(CLK), .clr(CLR));
  Register #(.width(1)) register_11 (.D(RWDOF), .en(1'b1), .Q(RWEX), .clk(CLK), .clr(CLR));
endmodule

module EX_WB (
  input  CLK,
  input  CLR,
  input  SLTEX,
  input  [1:0] MDEX,
  input  [4:0] DAEX,
  input  [31:0] FEX,
  input  RWEX,
  input  [31:0] MEMREADEX,
  input  EN,
  output STLWB,
  output [1:0] MDWB,
  output [4:0] DAWB,
  output [31:0] FWB,
  output RWWB,
  output [31:0] MEMREADWB
);

  Register #(.width(1)) register_1 (.D(SLTEX), .en(EN), .Q(STLWB), .clk(CLK), .clr(CLR));
  Register #(.width(32)) register_2 (.D(FEX), .en(EN), .Q(FWB), .clk(CLK), .clr(CLR));
  Register #(.width(32)) register_3 (.D(MEMREADEX), .en(EN), .Q(MEMREADWB), .clk(CLK), .clr(CLR));
  Register #(.width(2)) register_4 (.D(MDEX), .en(EN), .Q(MDWB), .clk(CLK), .clr(CLR));
  Register #(.width(5)) register_5 (.D(DAEX), .en(EN), .Q(DAWB), .clk(CLK), .clr(CLR));
  Register #(.width(1)) register_6 (.D(RWEX), .en(EN), .Q(RWWB), .clk(CLK), .clr(CLR));
endmodule

// Instruction Decoder
module Instruction_decoder (
  input  [31:0] Inst,
  output [4:0] BA,
  output [4:0] AA,
  output [4:0] DA,
  output [1:0] MD,
  output [1:0] BS,
  output MW,
  output [3:0] FS,
  output MA,
  output RW,
  output PS,
  output MB,
  output CS
);

  Opcode_decoder opcode_decoder_1 (
    .OP(Inst[31:25]), .MD(MD), .BS(BS), .MW(MW), .FS(FS), .MA(MA), .RW(RW), .PS(PS), .MB(MB), .CS(CS));

  assign AA = Inst[19:15];
  assign BA = Inst[14:10];
  assign DA = Inst[24:20];
endmodule

module Data_hazard (
  input  MADOF,
  input  MBDOF,
  input  [4:0] BADOF,
  input  [4:0] AADOF,
  input  [4:0] DAEX,
  input  RWEX,
  input  [4:0] DAWB,
  input  RWWB,
  output DHS
);

  wire and_1_out, and_2_out, and_3_out, and_4_out, comparator_1_eq, comparator_2_eq, comparator_3_eq,
       comparator_4_eq, not_1_out, not_2_out, or_1_out, or_2_out, or_3_out, or_4_out;

  Comparator #(.width(5)) comparator_1 (.a(DAEX), .b(AADOF), .eq(comparator_1_eq));  // open: gt, lt
  Comparator #(.width(5)) comparator_2 (.a(DAEX), .b(BADOF), .eq(comparator_2_eq));  // open: gt, lt
  or or_1 (or_1_out, DAEX[0], DAEX[1], DAEX[2], DAEX[3], DAEX[4]);
  Comparator #(.width(5)) comparator_3 (.a(DAWB), .b(AADOF), .eq(comparator_3_eq));  // open: gt, lt
  Comparator #(.width(5)) comparator_4 (.a(DAWB), .b(BADOF), .eq(comparator_4_eq));  // open: gt, lt
  or or_2 (or_2_out, DAWB[0], DAWB[1], DAWB[2], DAWB[3], DAWB[4]);
  not not_1 (not_1_out, MBDOF);
  not not_2 (not_2_out, MADOF);
  and and_1 (and_1_out, comparator_1_eq, not_2_out, RWEX, or_1_out);
  and and_2 (and_2_out, comparator_2_eq, not_1_out, RWEX, or_1_out);
  and and_3 (and_3_out, comparator_3_eq, not_2_out, RWWB, or_2_out);
  and and_4 (and_4_out, comparator_4_eq, not_1_out, RWWB, or_2_out);
  or or_3 (or_3_out, and_1_out, and_2_out);
  or or_4 (or_4_out, and_3_out, and_4_out);
  or or_5 (DHS, or_3_out, or_4_out);
endmodule

// Function unit
module Function_unit (
  input  [31:0] RA,
  input  [31:0] RB,
  input  [3:0] FS,
  input  [4:0] Shift,
  output N,
  output V,
  output Z,
  output [31:0] F
);

  wire adder_32bit_1_v, subtractor_32bit_1_v;
  wire [31:0] adder_32bit_1_out, and_1_out, not_1_out, or_1_out, shifter_1_out, shifter_2_out,
       subtractor_32bit_1_out, xor_1_out;

  assign and_1_out = RA & RB;  // AND_Gate and_1, 32 bits wide
  assign or_1_out = RA | RB;  // OR_Gate or_1, 32 bits wide
  assign xor_1_out = RA ^ RB;  // XOR_Gate xor_1, 32 bits wide
  assign not_1_out = ~RA;  // NOT_Gate not_1, 32 bits wide
  Shifter #(.width(32), .shift("lr")) shifter_1 (.in(RA), .\dist (Shift), .out(shifter_1_out));
  Shifter #(.width(32)) shifter_2 (.in(RA), .\dist (Shift), .out(shifter_2_out));
  Adder_32bit adder_32bit_1 (.V(adder_32bit_1_v), .RA(RA), .RB(RB), .OUT(adder_32bit_1_out));  // open: in_3
  Subtractor_32bit subtractor_32bit_1 (
    .V(subtractor_32bit_1_v), .RA(RA), .RB(RB), .OUT(subtractor_32bit_1_out));  // open: in_3
  Multiplexer #(.select(4), .enable("false")) multiplexer_1 (
    .in0(1'b0), .in1(1'b0), .in2(adder_32bit_1_v), .in3(1'b0), .in4(1'b0), .in5(subtractor_32bit_1_v),
    .in6(1'b0), .in7(1'b0), .in8(1'b0), .in9(1'b0), .in10(1'b0), .in11(1'b0), .in12(1'b0), .in13(1'b0),
    .in14(1'b0), .in15(1'b0), .out(V), .sel(FS));
  Multiplexer #(.select(4), .width(32)) multiplexer_2 (
    .in0(RA), .in1({32{1'b0}}), .in2(adder_32bit_1_out), .in3({32{1'b0}}), .in4({32{1'b0}}),
    .in5(subtractor_32bit_1_out), .in6({32{1'b0}}), .in7({32{1'b0}}), .in8(and_1_out), .in9(or_1_out),
    .in10(xor_1_out), .in11(not_1_out), .in12(RB), .in13(shifter_1_out), .in14(shifter_2_out),
    .in15({32{1'b0}}), .out(F), .sel(FS));  // open: en
  nor nor_1 (Z, F[0], F[1], F[2], F[3], F[4], F[5], F[6], F[7], F[8], F[9], F[10], F[11], F[12], F[13], F[14], F[15], F[16], F[17], F[18], F[19], F[20], F[21], F[22], F[23], F[24], F[25], F[26], F[27], F[28], F[29], F[30], F[31]);

  assign N = F[31];

  // Other names for the same wires on the sheet: A[31:0] = RA; B[31:0] = RB; S[3:0] = FS; SH[4:0] = Shift
endmodule

// Register file
module Register_file (
  input  [4:0] AA,
  input  [4:0] BA,
  input  [4:0] DA,
  input  RW,
  input  CLK,
  input  CLR,
  input  [31:0] DIN,
  output [31:0] RA,
  output [31:0] RB
);

  wire decoder_1_out0, decoder_1_out1, decoder_1_out2, decoder_1_out3, decoder_1_out4, decoder_1_out5,
       decoder_1_out6, decoder_1_out7, decoder_1_out8, decoder_1_out9, decoder_1_out10, decoder_1_out11,
       decoder_1_out12, decoder_1_out13, decoder_1_out14, decoder_1_out15, decoder_1_out16, decoder_1_out17,
       decoder_1_out18, decoder_1_out19, decoder_1_out20, decoder_1_out21, decoder_1_out22, decoder_1_out23,
       decoder_1_out24, decoder_1_out25, decoder_1_out26, decoder_1_out27, decoder_1_out28, decoder_1_out29,
       decoder_1_out30, decoder_1_out31;
  wire [31:0] R0_q, R1_q, R2_q, R3_q, R4_q, R5_q, R6_q, R7_q, R8_q, R9_q, R10_q, R11_q, R12_q, R13_q, R14_q,
       R15_q, R16_q, R17_q, R18_q, R19_q, R20_q, R21_q, R22_q, R23_q, R24_q, R25_q, R26_q, R27_q, R28_q,
       R29_q, R30_q, R31_q;

  Decoder #(.select(5)) decoder_1 (
    .out0(decoder_1_out0), .out1(decoder_1_out1), .out2(decoder_1_out2), .out3(decoder_1_out3),
    .out4(decoder_1_out4), .out5(decoder_1_out5), .out6(decoder_1_out6), .out7(decoder_1_out7),
    .out8(decoder_1_out8), .out9(decoder_1_out9), .out10(decoder_1_out10), .out11(decoder_1_out11),
    .out12(decoder_1_out12), .out13(decoder_1_out13), .out14(decoder_1_out14), .out15(decoder_1_out15),
    .out16(decoder_1_out16), .out17(decoder_1_out17), .out18(decoder_1_out18), .out19(decoder_1_out19),
    .out20(decoder_1_out20), .out21(decoder_1_out21), .out22(decoder_1_out22), .out23(decoder_1_out23),
    .out24(decoder_1_out24), .out25(decoder_1_out25), .out26(decoder_1_out26), .out27(decoder_1_out27),
    .out28(decoder_1_out28), .out29(decoder_1_out29), .out30(decoder_1_out30), .out31(decoder_1_out31),
    .sel(DA), .en(RW));
  Register #(.width(32)) R8 (.D(DIN), .en(decoder_1_out8), .Q(R8_q), .clk(CLK), .clr(CLR));
  Register #(.width(32)) R16 (.D(DIN), .en(decoder_1_out16), .Q(R16_q), .clk(CLK), .clr(CLR));
  Register #(.width(32)) R24 (.D(DIN), .en(decoder_1_out24), .Q(R24_q), .clk(CLK), .clr(CLR));
  Register #(.width(32)) R0 (.en(decoder_1_out0), .Q(R0_q), .clk(CLK), .clr(CLR));  // open: D
  Register #(.width(32)) R9 (.D(DIN), .en(decoder_1_out9), .Q(R9_q), .clk(CLK), .clr(CLR));
  Register #(.width(32)) R17 (.D(DIN), .en(decoder_1_out17), .Q(R17_q), .clk(CLK), .clr(CLR));
  Register #(.width(32)) R25 (.D(DIN), .en(decoder_1_out25), .Q(R25_q), .clk(CLK), .clr(CLR));
  Register #(.width(32)) R1 (.D(DIN), .en(decoder_1_out1), .Q(R1_q), .clk(CLK), .clr(CLR));
  Register #(.width(32)) R10 (.D(DIN), .en(decoder_1_out10), .Q(R10_q), .clk(CLK), .clr(CLR));
  Register #(.width(32)) R18 (.D(DIN), .en(decoder_1_out18), .Q(R18_q), .clk(CLK), .clr(CLR));
  Register #(.width(32)) R26 (.D(DIN), .en(decoder_1_out26), .Q(R26_q), .clk(CLK), .clr(CLR));
  Register #(.width(32)) R2 (.D(DIN), .en(decoder_1_out2), .Q(R2_q), .clk(CLK), .clr(CLR));
  Register #(.width(32)) R11 (.D(DIN), .en(decoder_1_out11), .Q(R11_q), .clk(CLK), .clr(CLR));
  Register #(.width(32)) R19 (.D(DIN), .en(decoder_1_out19), .Q(R19_q), .clk(CLK), .clr(CLR));
  Register #(.width(32)) R27 (.D(DIN), .en(decoder_1_out27), .Q(R27_q), .clk(CLK), .clr(CLR));
  Register #(.width(32)) R3 (.D(DIN), .en(decoder_1_out3), .Q(R3_q), .clk(CLK), .clr(CLR));
  Register #(.width(32)) R12 (.D(DIN), .en(decoder_1_out12), .Q(R12_q), .clk(CLK), .clr(CLR));
  Register #(.width(32)) R20 (.D(DIN), .en(decoder_1_out20), .Q(R20_q), .clk(CLK), .clr(CLR));
  Register #(.width(32)) R28 (.D(DIN), .en(decoder_1_out28), .Q(R28_q), .clk(CLK), .clr(CLR));
  Register #(.width(32)) R4 (.D(DIN), .en(decoder_1_out4), .Q(R4_q), .clk(CLK), .clr(CLR));
  Register #(.width(32)) R13 (.D(DIN), .en(decoder_1_out13), .Q(R13_q), .clk(CLK), .clr(CLR));
  Register #(.width(32)) R21 (.D(DIN), .en(decoder_1_out21), .Q(R21_q), .clk(CLK), .clr(CLR));
  Register #(.width(32)) R29 (.D(DIN), .en(decoder_1_out29), .Q(R29_q), .clk(CLK), .clr(CLR));
  Register #(.width(32)) R5 (.D(DIN), .en(decoder_1_out5), .Q(R5_q), .clk(CLK), .clr(CLR));
  Register #(.width(32)) R14 (.D(DIN), .en(decoder_1_out14), .Q(R14_q), .clk(CLK), .clr(CLR));
  Register #(.width(32)) R22 (.D(DIN), .en(decoder_1_out22), .Q(R22_q), .clk(CLK), .clr(CLR));
  Register #(.width(32)) R30 (.D(DIN), .en(decoder_1_out30), .Q(R30_q), .clk(CLK), .clr(CLR));
  Register #(.width(32)) R6 (.D(DIN), .en(decoder_1_out6), .Q(R6_q), .clk(CLK), .clr(CLR));
  Register #(.width(32)) R15 (.D(DIN), .en(decoder_1_out15), .Q(R15_q), .clk(CLK), .clr(CLR));
  Register #(.width(32)) R23 (.D(DIN), .en(decoder_1_out23), .Q(R23_q), .clk(CLK), .clr(CLR));
  Register #(.width(32)) R31 (.D(DIN), .en(decoder_1_out31), .Q(R31_q), .clk(CLK), .clr(CLR));
  Register #(.width(32)) R7 (.D(DIN), .en(decoder_1_out7), .Q(R7_q), .clk(CLK), .clr(CLR));
  Multiplexer #(.select(5), .width(32), .enable("false")) multiplexer_1 (
    .in0(R0_q), .in1(R1_q), .in2(R2_q), .in3(R3_q), .in4(R4_q), .in5(R5_q), .in6(R6_q), .in7(R7_q),
    .in8(R8_q), .in9(R9_q), .in10(R10_q), .in11(R11_q), .in12(R12_q), .in13(R13_q), .in14(R14_q),
    .in15(R15_q), .in16(R16_q), .in17(R17_q), .in18(R18_q), .in19(R19_q), .in20(R20_q), .in21(R21_q),
    .in22(R22_q), .in23(R23_q), .in24(R24_q), .in25(R25_q), .in26(R26_q), .in27(R27_q), .in28(R28_q),
    .in29(R29_q), .in30(R30_q), .in31(R31_q), .out(RA), .sel(AA));
  Multiplexer #(.select(5), .width(32), .enable("false")) multiplexer_2 (
    .in0(R0_q), .in1(R1_q), .in2(R2_q), .in3(R3_q), .in4(R4_q), .in5(R5_q), .in6(R6_q), .in7(R7_q),
    .in8(R8_q), .in9(R9_q), .in10(R10_q), .in11(R11_q), .in12(R12_q), .in13(R13_q), .in14(R14_q),
    .in15(R15_q), .in16(R16_q), .in17(R17_q), .in18(R18_q), .in19(R19_q), .in20(R20_q), .in21(R21_q),
    .in22(R22_q), .in23(R23_q), .in24(R24_q), .in25(R25_q), .in26(R26_q), .in27(R27_q), .in28(R28_q),
    .in29(R29_q), .in30(R30_q), .in31(R31_q), .out(RB), .sel(BA));

  // Other names for the same wires on the sheet: A_data[31:0] = RA; AS[4:0] = AA; B_data[31:0] = RB; BS[4:0] = BA;
  //   D_data[31:0] = DIN; Destination_select[4:0] = DA; Write_enable = RW
endmodule

module Constant_unit (
  input  CS,
  input  [14:0] Im_input,
  output [31:0] Im_output
);

  wire [31:0] bit_extender_1_out, bit_extender_2_out;

  assign bit_extender_1_out = {{17{1'b0}}, Im_input};  // Bit_Extender bit_extender_1
  assign bit_extender_2_out = {{17{Im_input[14]}}, Im_input};  // Bit_Extender bit_extender_2
  Multiplexer #(.width(32), .enable("false")) multiplexer_1 (
    .in0(bit_extender_1_out), .in1(bit_extender_2_out), .out(Im_output), .sel(CS));
endmodule
